# Fritzing sketch Schematic Arduino Nano to 1602 LCD (saved by Fritzing 0.9.10b)
circuit board: 16.1233cm x 9.11086cm
breadboards: 1

parts:
  LCD1 = LCD screen
  Onderdeel1 = Arduino Nano (Rev3.0)
  R1 = Trimmer Potentiometer [maximum_resistance=10kΩ knob_status=50% power=0.5W package=THT]

nets:
  VSS: LCD1.VSS, LCD1.R/W, LCD1.LED-, Onderdeel1.GND, R1.leg2
  VDD: LCD1.VDD, LCD1.LED+, Onderdeel1.5V, R1.leg1
  N1: LCD1.V0, R1.wiper
  N2: LCD1.RS, Onderdeel1.D7
  N3: LCD1.E, Onderdeel1.D8
  N4: LCD1.DB4, Onderdeel1.D9
  N5: LCD1.DB5, Onderdeel1.D10
  N6: LCD1.DB6, Onderdeel1.D11/MOSI
  N7: LCD1.DB7, Onderdeel1.D12/MISO

// code stored in the sketch: Untitled5.ino

